// Logisim project 24125102_3.circ as structural Verilog: 1 circuit, main circuit main
module main (
  input  in_1,
  input  in_2,
  input  in_3,
  input  in_4,
  input  in_5,
  input  in_6,
  input  in_7,
  input  in_8,
  input  in_9,
  output out_10,
  output out_11,
  output out_12,
  output out_13,
  output out_14
);

  wire nand_1_out, nand_4_out, nand_5_out, nand_6_out, nand_7_out, nand_8_out, nand_9_out, nand_10_out,
       nand_12_out, nand_13_out;

  nand nand_1 (nand_1_out, in_1, in_3);
  nand nand_2 (out_12, in_5, in_5);
  nand nand_3 (out_10, nand_1_out, nand_1_out);
  nand nand_4 (nand_4_out, in_8, in_9);
  nand nand_5 (nand_5_out, in_8, nand_4_out);
  nand nand_6 (nand_6_out, nand_4_out, in_9);
  nand nand_7 (nand_7_out, nand_5_out, nand_6_out);
  nand nand_8 (nand_8_out, in_2, in_2);
  nand nand_9 (nand_9_out, in_4, in_4);
  nand nand_10 (nand_10_out, in_6, in_7);
  nand nand_11 (out_14, nand_7_out, nand_7_out);
  nand nand_12 (nand_12_out, in_6, nand_10_out);
  nand nand_13 (nand_13_out, nand_10_out, in_7);
  nand nand_14 (out_11, nand_8_out, nand_9_out);
  nand nand_15 (out_13, nand_12_out, nand_13_out);

  // Notes on the sheet:
  //   AND using NAND gates
  //   NOT using NAND gates
  //   XNOR using NAND gates
  //   OR using NAND gates
  //   XOR using NAND gates
endmodule
