// Logisim project 24125102_4.circ as structural Verilog: 1 circuit, main circuit main
module main (
  input  in_1,
  input  in_2,
  input  in_3,
  input  in_4,
  input  in_5,
  input  in_6,
  input  in_7,
  output out_8,
  output out_9,
  output out_10,
  output out_11
);

  wire nor_1_out, nor_2_out, nor_5_out, nor_6_out, nor_7_out, nor_9_out, nor_10_out;

  nor nor_1 (nor_1_out, in_1, in_1);
  nor nor_2 (nor_2_out, in_4, in_4);
  nor nor_3 (out_10, in_5, in_5);
  nor nor_4 (out_8, nor_1_out, nor_2_out);
  nor nor_5 (nor_5_out, in_2, in_3);
  nor nor_6 (nor_6_out, in_6, in_6);
  nor nor_7 (nor_7_out, in_7, in_7);
  nor nor_8 (out_9, nor_5_out, nor_5_out);
  nor nor_9 (nor_9_out, nor_6_out, nor_7_out);
  nor nor_10 (nor_10_out, in_6, in_7);
  nor nor_11 (out_11, nor_9_out, nor_10_out);

  // Notes on the sheet:
  //   AND using NOR gates
  //   NOT using NOR gates
  //   XOR using NOR gates
  //   OR using NOR gates
endmodule
