// Logisim project 24125102_6.circ as structural Verilog: 1 circuit, main circuit main
module main (
  input  X3,
  input  X2,
  input  X1,
  input  X0,
  output out_5
);

  wire nand_1_out, nand_2_out, nand_3_out, nand_4_out, nand_5_out, nand_6_out, nand_7_out, nand_8_out,
       nand_9_out;

  nand nand_1 (nand_1_out, X0, X0);
  nand nand_2 (nand_2_out, X2, X0);
  nand nand_3 (nand_3_out, X2, nand_2_out);
  nand nand_4 (nand_4_out, nand_2_out, X0);
  nand nand_5 (nand_5_out, nand_1_out, X1);
  nand nand_6 (nand_6_out, X1, X1);
  nand nand_7 (nand_7_out, nand_3_out, nand_4_out);
  nand nand_8 (nand_8_out, nand_6_out, nand_7_out);
  nand nand_9 (nand_9_out, nand_5_out, nand_8_out);
  nand nand_10 (out_5, nand_9_out, nand_9_out);

  // Notes on the sheet:
  //   Note:  X3 value does not affect the output value
  //   Output 1 on 0000, 1000, 0101, 1101, 0111, 1111, 0011, or 1011. Otherwise output 0
endmodule
