// Logisim project 24125102_7.circ as structural Verilog: 1 circuit, main circuit main
module main (
  output out_1
);

  wire and_1_out, and_2_out, button_1_out, dipswitch_1_sw1, dipswitch_1_sw2, dipswitch_1_sw3,
       dipswitch_1_sw4, dipswitch_1_sw5, dipswitch_1_sw6, dipswitch_1_sw7, dipswitch_1_sw8, n7436_1_pin3,
       n7436_1_pin8, n7436_1_pin11, not_1_out;

  DipSwitch dipswitch_1 (
    .sw1(dipswitch_1_sw1), .sw2(dipswitch_1_sw2), .sw3(dipswitch_1_sw3), .sw4(dipswitch_1_sw4),
    .sw5(dipswitch_1_sw5), .sw6(dipswitch_1_sw6), .sw7(dipswitch_1_sw7), .sw8(dipswitch_1_sw8));
  _7436 u_7436_1 (
    .pin1(dipswitch_1_sw5), .pin2(dipswitch_1_sw6), .pin3(n7436_1_pin3), .pin13(dipswitch_1_sw4),
    .pin12(dipswitch_1_sw3), .pin11(n7436_1_pin11), .pin10(dipswitch_1_sw2), .pin9(dipswitch_1_sw1),
    .pin8(n7436_1_pin8));  // open: pin4, pin5, pin6
  Button button_1 (.out(button_1_out));
  not not_1 (not_1_out, dipswitch_1_sw8);
  and and_1 (and_1_out, dipswitch_1_sw7, not_1_out);
  and and_2 (and_2_out, n7436_1_pin11, n7436_1_pin8, and_1_out, n7436_1_pin3);
  and and_3 (out_1, and_2_out, button_1_out);

  // Notes on the sheet:
  //   Enter ID here (1: MSB, 8: LSB)
  //   Pass: 02 (00000010)
  //   Button
endmodule
