// Logisim project 24125102_8.circ as structural Verilog: 1 circuit, main circuit main
module main (
  output out_1
);

  wire dipswitch_1_sw1, dipswitch_1_sw2, dipswitch_1_sw3, dipswitch_1_sw4, dipswitch_1_sw5, dipswitch_1_sw6,
       dipswitch_1_sw7, xor_1_out, xor_2_out, xor_3_out, xor_4_out, xor_5_out;

  DipSwitch #(.number(7)) dipswitch_1 (
    .sw1(dipswitch_1_sw1), .sw2(dipswitch_1_sw2), .sw3(dipswitch_1_sw3), .sw4(dipswitch_1_sw4),
    .sw5(dipswitch_1_sw5), .sw6(dipswitch_1_sw6), .sw7(dipswitch_1_sw7));
  xor xor_1 (xor_1_out, dipswitch_1_sw1, dipswitch_1_sw2);
  xor xor_2 (xor_2_out, dipswitch_1_sw3, dipswitch_1_sw4);
  xor xor_3 (xor_3_out, dipswitch_1_sw5, dipswitch_1_sw6);
  xor xor_4 (xor_4_out, xor_1_out, xor_2_out);
  xor xor_5 (xor_5_out, xor_3_out, dipswitch_1_sw7);
  xor xor_6 (out_1, xor_4_out, xor_5_out);

  // Notes on the sheet:
  //   Even parity
  //   Input data here (1: MSB, 7: LSB)
endmodule
