// Logisim project 24125102_2.circ as structural Verilog: 1 circuit, main circuit main
module main (
);

  wire clock_1_out, d_ff_1_qn, d_ff_2_qn, d_ff_3_qn, d_ff_4_qn;
  wire [3:0] d_ff_1_q;

  D_Flip_Flop #(.trigger("falling")) d_ff_1 (
    .D(d_ff_1_qn), .clk(clock_1_out), .Q(d_ff_1_q[0]), .Qn(d_ff_1_qn));  // open: preset, reset
  Clock clock_1 (.out(clock_1_out));
  D_Flip_Flop #(.trigger("falling")) d_ff_2 (
    .D(d_ff_2_qn), .clk(d_ff_1_q[0]), .Q(d_ff_1_q[1]), .Qn(d_ff_2_qn));  // open: preset, reset
  D_Flip_Flop #(.trigger("falling")) d_ff_3 (
    .D(d_ff_3_qn), .clk(d_ff_1_q[1]), .Q(d_ff_1_q[2]), .Qn(d_ff_3_qn));  // open: preset, reset
  D_Flip_Flop #(.trigger("falling")) d_ff_4 (
    .D(d_ff_4_qn), .clk(d_ff_1_q[2]), .Q(d_ff_1_q[3]), .Qn(d_ff_4_qn));  // open: preset, reset
  // Binary_to_BCD_converter binary_to_bcd_converter_1: pin names not known
  // Digital_Oscilloscope digital_oscilloscope_1: pin names not known; wires that end beside it: clock_1_out, d_ff_1_q[0], d_ff_1_q[1], d_ff_1_q[2], d_ff_1_q[3]
  Hex_Digit_Display hex_digit_display_1 ();  // open: value, dp
  Hex_Digit_Display hex_digit_display_2 ();  // open: value, dp

  // Notes on the sheet:
  //   4-bit async counter using D flip-flops
endmodule
