// Logisim project 24125102_3.circ as structural Verilog: 1 circuit, main circuit main
module main (
);

  wire and_1_out, clock_1_out, j_k_ff_1_qn, j_k_ff_2_qn, j_k_ff_3_qn;
  wire [3:0] j_k_ff_1_q;

  Clock clock_1 (.out(clock_1_out));
  J_K_Flip_Flop j_k_ff_1 (
    .J(1'b1), .K(1'b1), .clk(clock_1_out), .Q(j_k_ff_1_q[0]), .Qn(j_k_ff_1_qn), .reset(and_1_out));  // open: preset
  J_K_Flip_Flop j_k_ff_2 (
    .J(1'b1), .K(1'b1), .clk(j_k_ff_1_qn), .Q(j_k_ff_1_q[1]), .Qn(j_k_ff_2_qn), .reset(and_1_out));  // open: preset
  J_K_Flip_Flop j_k_ff_3 (
    .J(1'b1), .K(1'b1), .clk(j_k_ff_2_qn), .Q(j_k_ff_1_q[2]), .Qn(j_k_ff_3_qn), .reset(and_1_out));  // open: preset
  J_K_Flip_Flop j_k_ff_4 (
    .J(1'b1), .K(1'b1), .clk(j_k_ff_3_qn), .Q(j_k_ff_1_q[3]), .reset(and_1_out));  // open: Qn, preset
  and and_1 (and_1_out, j_k_ff_1_q[0], j_k_ff_1_q[2], j_k_ff_1_q[3]);
  Hex_Digit_Display hex_digit_display_1 ();  // open: value, dp
  // Binary_to_BCD_converter binary_to_bcd_converter_1: pin names not known; wires that end beside it: {{5{1'b0}}, j_k_ff_1_q}
  Hex_Digit_Display hex_digit_display_2 ();  // open: value, dp

  // Notes on the sheet:
  //   2-bit async counter to 12 using JK flip-flops
endmodule
