// Logisim project 24125102_4.circ as structural Verilog: 1 circuit, main circuit main
module main (
);

  wire and_1_out, and_2_out, clock_1_out, d_ff_3_qn;
  wire [2:0] d_ff_1_q;

  D_Flip_Flop #(.trigger("falling")) d_ff_1 (
    .D(and_1_out), .clk(clock_1_out), .Q(d_ff_1_q[0]));  // open: Qn, preset, reset
  Clock clock_1 (.out(clock_1_out));
  and and_1 (and_1_out, d_ff_1_q[1], d_ff_3_qn);
  D_Flip_Flop #(.trigger("falling")) d_ff_2 (
    .D(d_ff_3_qn), .clk(clock_1_out), .Q(d_ff_1_q[1]));  // open: Qn, preset, reset
  and and_2 (and_2_out, d_ff_1_q[0], d_ff_3_qn);
  D_Flip_Flop #(.trigger("falling")) d_ff_3 (
    .D(and_2_out), .clk(clock_1_out), .Q(d_ff_1_q[2]), .Qn(d_ff_3_qn));  // open: preset, reset
  // Binary_to_BCD_converter binary_to_bcd_converter_1: pin names not known
  Hex_Digit_Display hex_digit_display_1 ();  // open: value, dp
  Hex_Digit_Display hex_digit_display_2 ();  // open: value, dp

  // Notes on the sheet:
  //   3-bit synchronous counter 0 -> 2 ->3 ->7 using D flip-flops
endmodule
