// Logisim project 24125102_5.circ as structural Verilog: 1 circuit, main circuit main
module main (
  input  Control
);

  wire and_1_out, and_2_out, and_3_out, and_4_out, and_5_out, and_6_out, and_7_out, and_8_out, clock_1_out,
       j_k_ff_1_qn, j_k_ff_2_qn, j_k_ff_3_qn, not_1_out, or_1_out, or_2_out, or_3_out, or_4_out, or_5_out,
       xnor_1_out, xnor_2_out;
  wire [2:0] j_k_ff_1_q;

  Clock clock_1 (.out(clock_1_out));
  and and_1 (and_1_out, Control, and_3_out);
  not not_1 (not_1_out, Control);
  and and_2 (and_2_out, and_6_out, not_1_out);
  and and_3 (and_3_out, j_k_ff_1_q[1], or_2_out);
  J_K_Flip_Flop j_k_ff_1 (
    .J(or_1_out), .K(or_1_out), .clk(clock_1_out), .Q(j_k_ff_1_q[0]), .Qn(j_k_ff_1_qn));  // open: preset, reset
  or or_1 (or_1_out, and_1_out, and_2_out);
  or or_2 (or_2_out, j_k_ff_1_q[2], j_k_ff_1_qn);
  and and_4 (and_4_out, Control, xnor_1_out);
  and and_5 (and_5_out, j_k_ff_1_qn, not_1_out);
  xnor xnor_1 (xnor_1_out, j_k_ff_1_q[2], j_k_ff_1_q[1]);
  J_K_Flip_Flop j_k_ff_2 (
    .J(or_3_out), .K(or_3_out), .clk(clock_1_out), .Q(j_k_ff_1_q[1]), .Qn(j_k_ff_2_qn));  // open: preset, reset
  or or_3 (or_3_out, and_4_out, and_5_out);
  or or_4 (or_4_out, j_k_ff_2_qn, j_k_ff_1_q[0]);
  and and_6 (and_6_out, or_4_out, j_k_ff_3_qn);
  and and_7 (and_7_out, Control, j_k_ff_1_q[0]);
  or or_5 (or_5_out, and_7_out, and_8_out);
  and and_8 (and_8_out, xnor_2_out, not_1_out);
  J_K_Flip_Flop j_k_ff_3 (
    .J(or_5_out), .K(or_5_out), .clk(clock_1_out), .Q(j_k_ff_1_q[2]), .Qn(j_k_ff_3_qn));  // open: preset, reset
  xnor xnor_2 (xnor_2_out, j_k_ff_1_q[2], j_k_ff_1_q[1]);
  // Binary_to_BCD_converter binary_to_bcd_converter_1: pin names not known
  Hex_Digit_Display hex_digit_display_1 ();  // open: value, dp
  Hex_Digit_Display hex_digit_display_2 ();  // open: value, dp

  // Notes on the sheet:
  //   Dual synchronous counter using JK flip-flop 0 -> 2 -> 3 -> 7
endmodule
