// Logisim project 24125102_6.circ as structural Verilog: 1 circuit, main circuit main
module main (
  input  in_1
);

  wire and_1_out, button_1_out, button_2_out, button_3_out, clock_1_out, counter_2_carry, counter_3_carry;
  wire [4:0] counter_1_q, Hour_out;
  wire [5:0] counter_2_q, counter_3_q, Minute_out, Second_out;

  and and_1 (and_1_out, counter_3_carry, counter_2_carry);
  Counter #(.max('h17), .width(5)) counter_1 (
    .load(button_1_out), .count(and_1_out), .clk(clock_1_out), .D(Hour_out), .Q(counter_1_q));  // open: clr, up, carry
  Counter #(.max('h3b), .width(6)) counter_2 (
    .load(button_2_out), .count(counter_3_carry), .clk(clock_1_out), .D(Minute_out), .carry(counter_2_carry),
    .Q(counter_2_q));  // open: clr, up
  Counter #(.max('h3b), .width(6)) counter_3 (
    .load(button_3_out), .count(in_1), .clk(clock_1_out), .D(Second_out), .carry(counter_3_carry),
    .Q(counter_3_q));  // open: clr, up
  _7_Segment_Display u_7_segment_display_1 ();  // open: g, f, a, b, e, d, c, dp
  // BCD_to_7_Segment_decoder bcd_to_7_segment_decoder_1: pin names not known
  // Binary_to_BCD_converter #(.binvalue(5)) binary_to_bcd_converter_1: pin names not known; wires that end beside it: counter_1_q
  Clock clock_1 (.out(clock_1_out));
  Slider #(.width(5)) Hour (.out(Hour_out));
  Slider #(.width(6)) Minute (.out(Minute_out));
  Slider #(.width(6)) Second (.out(Second_out));
  _7_Segment_Display u_7_segment_display_2 ();  // open: g, f, a, b, e, d, c, dp
  // BCD_to_7_Segment_decoder bcd_to_7_segment_decoder_2: pin names not known
  _7_Segment_Display u_7_segment_display_3 ();  // open: g, f, a, b, e, d, c, dp
  // BCD_to_7_Segment_decoder bcd_to_7_segment_decoder_3: pin names not known
  // Binary_to_BCD_converter #(.binvalue(6)) binary_to_bcd_converter_2: pin names not known; wires that end beside it: counter_2_q
  _7_Segment_Display u_7_segment_display_4 ();  // open: g, f, a, b, e, d, c, dp
  // BCD_to_7_Segment_decoder bcd_to_7_segment_decoder_4: pin names not known
  _7_Segment_Display u_7_segment_display_5 ();  // open: g, f, a, b, e, d, c, dp
  // BCD_to_7_Segment_decoder bcd_to_7_segment_decoder_5: pin names not known
  // Binary_to_BCD_converter #(.binvalue(6)) binary_to_bcd_converter_3: pin names not known; wires that end beside it: counter_3_q
  Button button_1 (.out(button_1_out));
  Button button_2 (.out(button_2_out));
  Button button_3 (.out(button_3_out));
  _7_Segment_Display u_7_segment_display_6 ();  // open: g, f, a, b, e, d, c, dp
  // BCD_to_7_Segment_decoder bcd_to_7_segment_decoder_6: pin names not known

  // Notes on the sheet:
  //   Digital clock using counters
  //   On-off switch
  //   To set time, hold the button
endmodule
